// Logisim project ALU Design.circ as structural Verilog: 1 circuit, main circuit main
module main (
  input  in_1
);

  wire and_1_out, and_2_out, and_3_out, and_4_out, and_5_out, and_6_out, and_7_out, and_8_out, and_9_out,
       and_10_out, and_11_out, and_12_out, and_13_out, and_14_out, and_15_out, and_16_out, and_17_out,
       and_18_out, and_19_out, and_20_out, and_21_out, and_22_out, and_23_out, and_24_out, and_25_out,
       and_26_out, and_27_out, and_28_out, and_29_out, and_30_out, and_31_out, and_32_out, and_33_out,
       and_34_out, and_35_out, and_36_out, and_37_out, and_39_out, and_40_out, and_41_out, and_42_out,
       and_43_out, and_44_out, and_45_out, and_46_out, and_47_out, and_48_out, and_49_out, and_50_out,
       Comp_out, dipswitch_1_sw1, dipswitch_1_sw2, dipswitch_1_sw3, dipswitch_1_sw4, dipswitch_2_sw1,
       dipswitch_2_sw2, dipswitch_2_sw3, dipswitch_2_sw4, dipswitch_3_sw1, dipswitch_3_sw2, n7447_1_pin2,
       n7447_1_pin6, n7447_1_pin9, n7447_1_pin10, n7447_1_pin11, n7447_1_pin12, n7447_1_pin13, n7447_1_pin14,
       n7447_1_pin15, n7447_2_pin9, n7447_2_pin10, n7447_2_pin11, n7447_2_pin12, n7447_2_pin13,
       n7447_2_pin14, n7447_2_pin15, not_1_out, not_2_out, not_3_out, not_4_out, not_5_out, not_6_out,
       not_7_out, not_8_out, not_9_out, not_10_out, not_11_out, not_12_out, not_13_out, not_14_out,
       not_15_out, not_16_out, not_17_out, not_18_out, not_19_out, not_20_out, not_21_out, not_22_out,
       not_23_out, not_24_out, not_25_out, not_26_out, not_27_out, not_28_out, not_29_out, not_30_out,
       not_31_out, not_32_out, or_1_out, or_2_out, or_3_out, or_4_out, or_5_out, or_6_out, or_7_out,
       or_8_out, or_9_out, or_10_out, or_11_out, or_12_out, or_13_out, or_14_out, or_15_out, or_16_out,
       or_17_out, or_18_out, or_19_out, or_20_out, or_22_out, or_23_out, or_24_out, or_25_out, or_26_out,
       or_27_out, or_28_out, or_29_out, or_30_out, or_31_out, or_32_out, or_33_out, Subt_out, xor_1_out,
       xor_2_out, xor_3_out, xor_4_out, xor_5_out, xor_6_out, xor_7_out, xor_8_out, xor_9_out, xor_10_out,
       xor_11_out, xor_12_out, xor_13_out, xor_14_out, xor_15_out, xor_16_out, xor_17_out, xor_18_out,
       xor_19_out, xor_20_out, xor_21_out, xor_22_out, xor_23_out, xor_24_out, xor_25_out, xor_26_out,
       xor_27_out, xor_28_out, xor_29_out, xor_30_out, xor_31_out, xor_32_out, xor_33_out, xor_34_out,
       xor_35_out, xor_36_out, xor_37_out, xor_38_out;

  DipSwitch dipswitch_1 (
    .sw1(dipswitch_1_sw1), .sw2(dipswitch_1_sw2), .sw3(dipswitch_1_sw3), .sw4(dipswitch_1_sw4));  // open: sw5, sw6, sw7, sw8
  xor xor_1 (xor_1_out, dipswitch_1_sw1, dipswitch_1_sw4);
  xor xor_2 (xor_2_out, dipswitch_1_sw1, dipswitch_1_sw3);
  DipSwitch dipswitch_2 (
    .sw1(dipswitch_2_sw1), .sw2(dipswitch_2_sw2), .sw3(dipswitch_2_sw3), .sw4(dipswitch_2_sw4));  // open: sw5, sw6, sw7, sw8
  or or_1 (or_1_out, dipswitch_1_sw3, dipswitch_1_sw4);
  xor xor_3 (xor_3_out, dipswitch_1_sw1, xor_1_out);
  and and_1 (and_1_out, dipswitch_1_sw1, xor_1_out);
  xor xor_4 (xor_4_out, dipswitch_1_sw1, dipswitch_1_sw2);
  or or_2 (or_2_out, or_1_out, dipswitch_1_sw2);
  and and_2 (and_2_out, or_2_out, dipswitch_1_sw1);
  xor xor_5 (xor_5_out, xor_2_out, and_1_out);
  and and_3 (and_3_out, xor_2_out, and_1_out);
  xor xor_6 (xor_6_out, dipswitch_2_sw1, dipswitch_2_sw4);
  xor xor_7 (xor_7_out, dipswitch_2_sw1, dipswitch_2_sw3);
  xor xor_8 (xor_8_out, xor_4_out, and_3_out);
  DipSwitch dipswitch_3 (.sw1(dipswitch_3_sw1), .sw2(dipswitch_3_sw2));  // open: sw3, sw4, sw5, sw6, sw7, sw8
  xor xor_9 (xor_9_out, dipswitch_2_sw1, xor_6_out);
  and and_4 (and_4_out, dipswitch_2_sw1, xor_6_out);
  xor xor_10 (xor_10_out, dipswitch_2_sw1, dipswitch_2_sw2);
  or or_3 (or_3_out, dipswitch_2_sw4, dipswitch_2_sw3);
  or or_4 (or_4_out, Comp_out, or_33_out);
  xor xor_11 (xor_11_out, xor_7_out, and_4_out);
  and and_5 (and_5_out, xor_7_out, and_4_out);
  or or_5 (or_5_out, or_3_out, dipswitch_2_sw2);
  _7_Segment_Display u_7_segment_display_1 (
    .g(or_4_out), .f(Comp_out), .a(Comp_out), .b(Comp_out), .e(Comp_out), .c(Comp_out));  // open: d, dp
  _7_Segment_Display u_7_segment_display_2 (
    .g(or_14_out), .f(and_48_out), .a(and_44_out), .b(and_43_out), .e(or_24_out), .d(or_15_out), .c(or_22_out));  // open: dp
  not not_1 (not_1_out, dipswitch_3_sw1);
  not not_2 (not_2_out, dipswitch_3_sw2);
  xor xor_12 (xor_12_out, xor_10_out, and_5_out);
  and and_6 (and_6_out, dipswitch_2_sw1, or_5_out);
  _7_Segment_Display u_7_segment_display_3 (
    .g(or_9_out), .f(or_10_out), .a(or_11_out), .b(or_13_out), .e(or_6_out), .d(or_7_out), .c(or_8_out));  // open: dp
  and Comp (Comp_out, dipswitch_3_sw2, not_1_out);
  and Subt (Subt_out, dipswitch_3_sw1, not_2_out);
  or or_6 (or_6_out, Comp_out, not_10_out);
  xor xor_13 (xor_13_out, Subt_out, and_6_out);
  xor xor_14 (xor_14_out, Subt_out, xor_12_out);
  xor xor_15 (xor_15_out, Subt_out, xor_11_out);
  xor xor_16 (xor_16_out, Subt_out, xor_9_out);
  or or_7 (or_7_out, Comp_out, not_11_out);
  or or_8 (or_8_out, Comp_out, not_12_out);
  xor xor_17 (xor_17_out, xor_16_out, xor_3_out);
  or or_9 (or_9_out, Comp_out, not_15_out);
  or or_10 (or_10_out, Comp_out, not_20_out);
  not not_3 (not_3_out, xor_13_out);
  not not_4 (not_4_out, and_2_out);
  and and_7 (and_7_out, xor_16_out, xor_3_out);
  and and_8 (and_8_out, xor_17_out, Subt_out);
  or or_11 (or_11_out, Comp_out, not_17_out);
  and and_9 (and_9_out, and_2_out, not_3_out);
  xor xor_18 (xor_18_out, xor_13_out, and_2_out);
  not not_5 (not_5_out, xor_18_out);
  and and_10 (and_10_out, not_4_out, xor_13_out);
  xor xor_19 (xor_19_out, xor_17_out, Subt_out);
  or or_12 (or_12_out, and_7_out, and_8_out);
  xor xor_20 (xor_20_out, xor_19_out, or_33_out);
  or or_13 (or_13_out, Comp_out, not_16_out);
  or or_14 (or_14_out, Comp_out, not_29_out);
  or or_15 (or_15_out, Comp_out, not_26_out);
  xor xor_21 (xor_21_out, xor_15_out, xor_5_out);
  xor xor_22 (xor_22_out, or_33_out, xor_20_out);
  not not_6 (not_6_out, xor_14_out);
  not not_7 (not_7_out, xor_8_out);
  and and_11 (and_11_out, xor_15_out, xor_5_out);
  and and_12 (and_12_out, xor_21_out, or_12_out);
  and and_13 (and_13_out, or_33_out, xor_20_out);
  and and_14 (and_14_out, xor_8_out, not_6_out);
  xor xor_23 (xor_23_out, xor_14_out, xor_8_out);
  not not_8 (not_8_out, xor_23_out);
  and and_15 (and_15_out, not_7_out, xor_14_out);
  xor xor_24 (xor_24_out, xor_21_out, or_12_out);
  or or_16 (or_16_out, and_11_out, and_12_out);
  not not_9 (not_9_out, Comp_out);
  and and_16 (and_16_out, not_5_out, and_14_out);
  and and_17 (and_17_out, not_8_out, not_5_out);
  and and_18 (and_18_out, and_15_out, not_5_out);
  xor xor_25 (xor_25_out, xor_24_out, or_33_out);
  not not_10 (not_10_out, n7447_1_pin9);
  xor xor_26 (xor_26_out, xor_14_out, xor_8_out);
  and and_19 (and_19_out, xor_27_out, not_24_out);
  not not_11 (not_11_out, n7447_1_pin10);
  not not_12 (not_12_out, n7447_1_pin11);
  not not_13 (not_13_out, xor_15_out);
  not not_14 (not_14_out, xor_5_out);
  and and_20 (and_20_out, xor_14_out, xor_8_out);
  and and_21 (and_21_out, xor_26_out, or_16_out);
  xor xor_27 (xor_27_out, xor_25_out, and_13_out);
  and and_22 (and_22_out, xor_31_out, xor_35_out);
  or or_17 (or_17_out, and_19_out, and_26_out);
  or or_18 (or_18_out, or_17_out, and_45_out);
  not not_15 (not_15_out, n7447_1_pin14);
  not not_16 (not_16_out, n7447_1_pin12);
  not not_17 (not_17_out, n7447_1_pin13);
  and and_23 (and_23_out, xor_5_out, not_13_out);
  xor xor_28 (xor_28_out, xor_15_out, xor_5_out);
  not not_18 (not_18_out, xor_28_out);
  and and_24 (and_24_out, not_14_out, xor_15_out);
  xor xor_29 (xor_29_out, xor_26_out, or_16_out);
  or or_19 (or_19_out, and_20_out, and_21_out);
  and and_25 (and_25_out, xor_25_out, and_13_out);
  not not_19 (not_19_out, xor_27_out);
  and and_26 (and_26_out, and_22_out, not_19_out);
  _7447 u_7447_1 (
    .pin1(or_18_out), .pin2(n7447_1_pin2), .pin6(n7447_1_pin6), .pin7(xor_22_out), .pin15(n7447_1_pin15),
    .pin14(n7447_1_pin14), .pin13(n7447_1_pin13), .pin12(n7447_1_pin12), .pin11(n7447_1_pin11),
    .pin10(n7447_1_pin10), .pin9(n7447_1_pin9));  // open: pin3, pin4, pin5
  not not_20 (not_20_out, n7447_1_pin15);
  and and_27 (and_27_out, and_17_out, and_23_out);
  and and_28 (and_28_out, not_18_out, and_17_out);
  and and_29 (and_29_out, and_24_out, and_17_out);
  xor xor_30 (xor_30_out, xor_29_out, or_33_out);
  xor xor_31 (xor_31_out, xor_30_out, and_25_out);
  or or_20 (or_20_out, xor_27_out, not_24_out);
  and and_30 (and_30_out, or_20_out, xor_31_out);
  or or_21 (n7447_1_pin2, and_30_out, and_45_out);
  or or_22 (or_22_out, and_41_out, and_46_out);
  not not_21 (not_21_out, xor_16_out);
  not not_22 (not_22_out, xor_3_out);
  xor xor_32 (xor_32_out, xor_13_out, and_2_out);
  and and_31 (and_31_out, xor_13_out, and_2_out);
  and and_32 (and_32_out, xor_32_out, or_19_out);
  and and_33 (and_33_out, xor_30_out, and_25_out);
  and and_34 (and_34_out, xor_3_out, not_21_out);
  and and_35 (and_35_out, not_22_out, xor_16_out);
  xor xor_33 (xor_33_out, xor_32_out, or_19_out);
  and and_36 (and_36_out, and_28_out, and_34_out);
  and and_37 (and_37_out, and_35_out, and_28_out);
  or or_23 (or_23_out, and_31_out, and_32_out);
  xor xor_34 (xor_34_out, xor_33_out, or_33_out);
  xor xor_35 (xor_35_out, xor_34_out, and_33_out);
  not not_23 (not_23_out, or_31_out);
  and and_38 (n7447_1_pin6, xor_35_out, not_23_out);
  or or_24 (or_24_out, and_40_out, and_47_out);
  or or_25 (or_25_out, and_10_out, and_16_out);
  or or_26 (or_26_out, and_27_out, and_36_out);
  or or_27 (or_27_out, and_37_out, and_29_out);
  or or_28 (or_28_out, and_18_out, and_9_out);
  and and_39 (and_39_out, xor_34_out, and_33_out);
  not not_24 (not_24_out, xor_35_out);
  not not_25 (not_25_out, n7447_2_pin9);
  and and_40 (and_40_out, not_25_out, not_9_out);
  or or_29 (or_29_out, or_25_out, or_26_out);
  or or_30 (or_30_out, or_27_out, or_28_out);
  xor xor_36 (xor_36_out, or_23_out, or_33_out);
  not not_26 (not_26_out, n7447_2_pin10);
  not not_27 (not_27_out, n7447_2_pin12);
  not not_28 (not_28_out, n7447_2_pin11);
  and and_41 (and_41_out, not_28_out, not_9_out);
  xor xor_37 (xor_37_out, or_23_out, or_19_out);
  xor xor_38 (xor_38_out, xor_36_out, and_39_out);
  or or_31 (or_31_out, xor_27_out, xor_31_out);
  and and_42 (and_42_out, xor_35_out, or_31_out);
  or or_32 (or_32_out, and_42_out, and_45_out);
  not not_29 (not_29_out, n7447_2_pin14);
  not not_30 (not_30_out, n7447_2_pin13);
  and and_43 (and_43_out, not_27_out, not_9_out);
  and and_44 (and_44_out, not_30_out, not_9_out);
  and and_45 (and_45_out, xor_38_out, xor_37_out);
  _7447 u_7447_2 (
    .pin1(in_1), .pin2(in_1), .pin6(in_1), .pin7(or_32_out), .pin15(n7447_2_pin15), .pin14(n7447_2_pin14),
    .pin13(n7447_2_pin13), .pin12(n7447_2_pin12), .pin11(n7447_2_pin11), .pin10(n7447_2_pin10),
    .pin9(n7447_2_pin9));  // open: pin3, pin4, pin5
  not not_31 (not_31_out, n7447_2_pin15);
  and and_46 (and_46_out, or_29_out, Comp_out);
  and and_47 (and_47_out, Comp_out, or_30_out);
  not not_32 (not_32_out, xor_37_out);
  and and_48 (and_48_out, not_31_out, not_9_out);
  and and_49 (and_49_out, or_23_out, xor_37_out);
  and and_50 (and_50_out, not_32_out, xor_33_out);
  or or_33 (or_33_out, and_49_out, and_50_out);

  // Notes on the sheet:
  //   A
  //   B
  //   Op
  //   A1
  //   1's complement
  //   2's complement
  //   A=B
  //   B2
  //   B1
  //   A2
  //   1's complement
  //   B3
  //   F1
  //   A>B
  //   A<B
  //   C1
  //   2's complement
  //   H1
  //   A3
  //   F2
  //   G1
  //   1,2 =
  //   C2
  //   B4
  //   A1
  //   H2
  //   G2
  //   B1
  //   F3
  //   1,2,3 =
  //   A4
  //   C3
  //   G3
  //   H3
  //   F4
  //   G4
  //   C4
  //   F5(C4)
  //   H4
  //   overflow check
  //   A>B
  //   A<B
  //   H5
  //   J1
  //   negative check
  //   sign
endmodule
